# Fritzing sketch Wiring (saved by Fritzing 0.9.3b)

parts:
  Part1 = Arduino Uno (Rev3)
  S1 = Pushbutton [package="[THT]"]
  J1 = female pin header, 3 pins [form="♀ (female)"]
  J2 = male pin header, 5 pins [form="♂ (male)"]
  J3 = male pin header, 1 pin [form="♂ (male)"]
  J4 = male pin header, 4 pins [form="♂ (male)"]  # not connected

nets:
  N1: Part1.GND, S1.Pin_3, S1.Pin_4, J1.pin3, J2.pin4
  N2: Part1.D2, S1.Pin_1, S1.Pin_2
  N3: Part1.D3_PWM, J3.pin1
  N4: Part1.D6_PWM, J1.pin2
  N5: Part1.5V, J1.pin1
  N6: Part1.VIN, J2.pin1

notes:
  Halos cable
  (grey at top)
  USB2 header (GND left)
  GND when asleep
  push button
  (case reset)
